// Logisim project Beginners_Tutorial.circ as structural Verilog: 1 circuit, main circuit main
module main (
  input  in_1,
  input  X,
  input  Y,
  input  in_4,
  input  in_5,
  input  in_6,
  input  in_7,
  input  in_8,
  input  in_9,
  input  in_10,
  input  in_11,
  input  in_12,
  input  in_13,
  output out_14,
  output out_15,
  output out_16,
  output Cout,
  output out_18,
  output out_19,
  output out_20,
  output out_21,
  output out_22,
  output out_23,
  output out_24,
  output out_25,
  output out_26
);

  wire AND1_out, AND2_out, and_1_out, and_2_out, and_3_out, and_4_out, and_5_out, and_6_out, and_7_out,
       and_8_out, and_9_out, and_10_out, and_11_out, and_12_out, and_13_out, and_14_out, and_15_out,
       and_16_out, and_17_out, clock_1_out, d_ff_1_q, d_ff_2_q, d_ff_4_qn, dipswitch_1_p1, dipswitch_1_p2,
       dipswitch_1_p3, dipswitch_1_p4, dipswitch_1_p5, dipswitch_2_p1, dipswitch_2_p2, dipswitch_2_p3,
       not_1_out, not_2_out, not_3_out, not_4_out, OR1_out, or_3_out, or_4_out, or_5_out, or_6_out, or_7_out,
       or_8_out, xor_1_out, xor_3_out, xor_5_out, xor_7_out, xor_9_out, xor_11_out, xor_13_out, xor_15_out;

  or or_1 (Cout, and_1_out, and_2_out);
  or or_2 (out_22, and_3_out, and_4_out);
  and AND1 (AND1_out, X, not_1_out);
  not not_1 (not_1_out, Y);
  not not_2 (not_2_out, X);
  and AND2 (AND2_out, not_2_out, Y);
  and and_1 (and_1_out, in_5, in_4);
  and and_2 (and_2_out, xor_1_out, or_3_out);
  and and_3 (and_3_out, dipswitch_1_p5, dipswitch_1_p1);
  and and_4 (and_4_out, xor_3_out, or_4_out);
  xor xor_1 (xor_1_out, in_4, in_5);
  xor xor_2 (out_18, xor_1_out, or_3_out);
  xor xor_3 (xor_3_out, dipswitch_1_p1, dipswitch_1_p5);
  or OR1 (OR1_out, AND1_out, AND2_out);
  D_Flip_Flop d_ff_1 (.D(OR1_out), .clk(clock_1_out), .Q(d_ff_1_q));  // open: Qn, preset, reset
  Clock clock_1 (.out(clock_1_out));
  or or_3 (or_3_out, and_5_out, and_6_out);
  or or_4 (or_4_out, and_7_out, and_8_out);
  xor xor_4 (out_23, xor_3_out, or_4_out);
  // Probe on OR1_out
  not not_3 (not_3_out, clock_1_out);
  and and_5 (and_5_out, in_7, in_6);
  and and_6 (and_6_out, xor_5_out, or_5_out);
  and and_7 (and_7_out, dipswitch_2_p1, dipswitch_1_p2);
  and and_8 (and_8_out, xor_7_out, or_6_out);
  // Probe on d_ff_1_q
  D_Flip_Flop d_ff_2 (.D(d_ff_1_q), .clk(not_3_out), .Q(d_ff_2_q));  // open: Qn, preset, reset
  xor xor_5 (xor_5_out, in_6, in_7);
  // Probe on d_ff_2_q
  D_Flip_Flop d_ff_3 (.D(d_ff_2_q), .clk(clock_1_out), .Q(out_15), .Qn(out_16));  // open: preset, reset
  or or_5 (or_5_out, and_9_out, and_10_out);
  xor xor_6 (out_19, xor_5_out, or_5_out);
  or or_6 (or_6_out, and_11_out, and_12_out);
  xor xor_7 (xor_7_out, dipswitch_1_p2, dipswitch_2_p1);
  xor xor_8 (out_24, xor_7_out, or_6_out);
  // Probe on out_15
  and and_9 (and_9_out, in_9, in_8);
  and and_10 (and_10_out, xor_9_out, or_7_out);
  // DipSwitch #(.number(4)) dipswitch_1: pin names not known; wires that end beside it: dipswitch_1_p1, dipswitch_1_p2, dipswitch_1_p3, dipswitch_1_p4, dipswitch_1_p5
  // DipSwitch #(.number(4)) dipswitch_2: pin names not known; wires that end beside it: dipswitch_2_p1, dipswitch_2_p2, dipswitch_2_p3
  and and_11 (and_11_out, dipswitch_2_p2, dipswitch_1_p3);
  and and_12 (and_12_out, xor_11_out, or_8_out);
  or or_7 (or_7_out, and_13_out, and_14_out);
  xor xor_9 (xor_9_out, in_8, in_9);
  xor xor_10 (out_20, xor_9_out, or_7_out);
  xor xor_11 (xor_11_out, dipswitch_1_p3, dipswitch_2_p2);
  xor xor_12 (out_25, xor_11_out, or_8_out);
  or or_8 (or_8_out, and_15_out, and_16_out);
  not not_4 (not_4_out, in_1);
  and and_13 (and_13_out, in_11, in_10);
  and and_14 (and_14_out, xor_13_out, in_12);
  and and_15 (and_15_out, dipswitch_2_p3, dipswitch_1_p4);
  and and_16 (and_16_out, xor_15_out, in_13);
  and and_17 (and_17_out, not_4_out, in_1);
  xor xor_13 (xor_13_out, in_10, in_11);
  xor xor_14 (out_21, xor_13_out, in_12);
  xor xor_15 (xor_15_out, dipswitch_1_p4, dipswitch_2_p3);
  xor xor_16 (out_26, xor_15_out, in_13);
  D_Flip_Flop d_ff_4 (.D(d_ff_4_qn), .clk(and_17_out), .Q(out_14), .Qn(d_ff_4_qn));  // open: preset, reset

  // Notes on the sheet:
  //   Cout
  //   d4
  //   b3
  //   a3
  //   b3
  //   d3
  //   a3
  //   X xor Y
  //   b2
  //   b2
  //   d2
  //   a2
  //   B
  //   a2
  //   4-bit Adder
  //   A
  //   b1
  //   b1
  //   a1
  //   a1
  //   d1
  //   b0
  //   a0
  //   b0
  //   a0
  //   d0
  //   Ctrl-e and ctrl-I
  //   Cin
  //   Cin
endmodule
