// Logisim project DFlipFlopCircuit.circ as structural Verilog: 3 circuits, main circuit DFlipFlop
module DFlipFlop (
  input  D,
  input  En,
  output Q,
  output Qn
);

  wire dlatch_1_q, dlatch_1_qn, not_1_out;

  not not_1 (not_1_out, En);
  DLatch dlatch_1 (.D(D), .En(not_1_out), .Q(dlatch_1_q), .Qn(dlatch_1_qn));
  // NoConnect on dlatch_1_qn
  DLatch dlatch_2 (.D(dlatch_1_q), .En(En), .Q(Q), .Qn(Qn));
endmodule

module DLatch (
  input  D,
  input  En,
  output Q,
  output Qn
);

  wire and_1_out, and_2_out, not_1_out;

  not not_1 (not_1_out, D);
  and and_1 (and_1_out, D, En);
  and and_2 (and_2_out, En, not_1_out);
  nor nor_1 (Q, and_1_out, Qn);
  nor nor_2 (Qn, Q, and_2_out);
endmodule

module SRLatch (
  input  R,
  input  S,
  output Q,
  output Qn
);

  nor nor_1 (Q, R, Qn);
  nor nor_2 (Qn, Q, S);
endmodule
