// Logisim project FullAdder.circ as structural Verilog: 4 circuits, main circuit FullAdder32
module FullAdder32 (
  input  Cin,
  input  [31:0] X,
  input  [31:0] Y,
  output [31:0] S,
  output Cout
);

  wire fulladder8_1_cout, fulladder8_2_cout, fulladder8_3_cout;

  FullAdder8 fulladder8_1 (.Y(Y[7:0]), .X(X[7:0]), .Cin(Cin), .Cout(fulladder8_1_cout), .S(S[7:0]));
  FullAdder8 fulladder8_2 (.Y(Y[15:8]), .X(X[15:8]), .Cin(fulladder8_1_cout), .Cout(fulladder8_2_cout), .S(S[15:8]));
  FullAdder8 fulladder8_3 (.Y(Y[23:16]), .X(X[23:16]), .Cin(fulladder8_2_cout), .Cout(fulladder8_3_cout), .S(S[23:16]));
  FullAdder8 fulladder8_4 (.Y(Y[31:24]), .X(X[31:24]), .Cin(fulladder8_3_cout), .Cout(Cout), .S(S[31:24]));
endmodule

module FullAdder1 (
  input  X,
  input  Y,
  input  Cin,
  output Cout,
  output S
);

  wire and_1_out, and_2_out, xor_1_out, xor_2_out;

  or or_1 (Cout, and_1_out, and_2_out);
  and and_1 (and_1_out, X, Y);
  and and_2 (and_2_out, xor_1_out, Cin);
  xor xor_1 (xor_1_out, X, Y);
  xor xor_2 (xor_2_out, X, Y);
  xor xor_3 (S, xor_2_out, Cin);

  // Notes on the sheet:
  //   Cout = X*Y + (X ^ Y)*Cin
  //   S = X ^ Y ^ Cin
endmodule

module FullAdder8 (
  input  Cin,
  input  [7:0] X,
  input  [7:0] Y,
  output [7:0] S,
  output Cout
);

  wire fulladder1_1_cout, fulladder1_2_cout, fulladder1_3_cout, fulladder1_4_cout, fulladder1_5_cout,
       fulladder1_6_cout, fulladder1_7_cout;

  FullAdder1 fulladder1_1 (.X(X[0]), .Y(Y[0]), .Cin(Cin), .Cout(fulladder1_1_cout), .S(S[0]));
  FullAdder1 fulladder1_2 (.X(X[1]), .Y(Y[1]), .Cin(fulladder1_1_cout), .Cout(fulladder1_2_cout), .S(S[1]));
  FullAdder1 fulladder1_3 (.X(X[2]), .Y(Y[2]), .Cin(fulladder1_2_cout), .Cout(fulladder1_3_cout), .S(S[2]));
  FullAdder1 fulladder1_4 (.X(X[3]), .Y(Y[3]), .Cin(fulladder1_3_cout), .Cout(fulladder1_4_cout), .S(S[3]));
  FullAdder1 fulladder1_5 (.X(X[4]), .Y(Y[4]), .Cin(fulladder1_4_cout), .Cout(fulladder1_5_cout), .S(S[4]));
  FullAdder1 fulladder1_6 (.X(X[5]), .Y(Y[5]), .Cin(fulladder1_5_cout), .Cout(fulladder1_6_cout), .S(S[5]));
  FullAdder1 fulladder1_7 (.X(X[6]), .Y(Y[6]), .Cin(fulladder1_6_cout), .Cout(fulladder1_7_cout), .S(S[6]));
  FullAdder1 fulladder1_8 (.X(X[7]), .Y(Y[7]), .Cin(fulladder1_7_cout), .Cout(Cout), .S(S[7]));
endmodule

module FullAdder16 (
  input  [15:0] X,
  input  [15:0] Y,
  output [15:0] S,
  output Cout
);

  wire fulladder8_1_cout, undriven;

  // NoConnect on undriven
  FullAdder8 fulladder8_1 (.Y(Y[7:0]), .X(X[7:0]), .Cin(undriven), .Cout(fulladder8_1_cout), .S(S[7:0]));
  FullAdder8 fulladder8_2 (.Y(Y[15:8]), .X(X[15:8]), .Cin(fulladder8_1_cout), .Cout(Cout), .S(S[15:8]));
endmodule
