// Logisim project ProcessorDatapath2.circ as structural Verilog: 6 circuits, main circuit main
module main (
  input  in_1
);

  wire alu_1_zero, ALUSrc, Clk, MemRead, MemToReg, MemWrite, PCSrc, RegDst, RegWrite, switch_1_p2;
  wire [2:0] ALUOp;
  wire [4:0] instructionmem_1_i15to11, instructionmem_1_i20to16, instructionmem_1_i25to21, multiplexer_1_out;
  wire [7:0] controlled_buffer_2_out, controlled_buffer_2_out_2, controlled_buffer_2_out_3,
       controlled_buffer_2_out_4;
  wire [11:0] instructionmem_1_i31to26and5to0;
  wire [15:0] instructionmem_1_i15to0, pc_1_address;
  wire [31:0] alu_1_result, bit_extender_1_out, controlled_buffer_1_out, multiplexer_2_out,
       registerfile_1_readreg1, registerfile_1_readreg2, WriteData;

  // Switch switch_1: pin names not known; wires that end beside it: 1'b1, switch_1_p2
  Pull_Resistor pull_resistor_1 (.node(switch_1_p2));
  Clock clock_1 (.out(Clk));
  PC pc_1 (
    .PCSrc(PCSrc), .Clock(Clk), .Reset(switch_1_p2), .BranchAddr(instructionmem_1_i15to0),
    .Address(pc_1_address));
  // Probe on instructionmem_1_i31to26and5to0
  // Probe on pc_1_address
  InstructionMem instructionmem_1 (
    .Address(pc_1_address), .i31to26and5to0(instructionmem_1_i31to26and5to0),
    .i15To0(instructionmem_1_i15to0), .i15to11(instructionmem_1_i15to11), .i20to16(instructionmem_1_i20to16),
    .i25to21(instructionmem_1_i25to21));
  // Probe on instructionmem_1_i25to21
  // Probe on instructionmem_1_i20to16
  // Probe on instructionmem_1_i15to11
  assign bit_extender_1_out = {{16{instructionmem_1_i15to0[15]}}, instructionmem_1_i15to0};  // Bit_Extender bit_extender_1
  Multiplexer #(.width(5)) multiplexer_1 (
    .in0(instructionmem_1_i20to16), .in1(instructionmem_1_i15to11), .out(multiplexer_1_out), .sel(RegDst));
  // Probe on bit_extender_1_out
  Control control_1 (
    .OPCODEFUNC(instructionmem_1_i31to26and5to0), .Zero(alu_1_zero), .ALUOp(ALUOp), .RegDst(RegDst),
    .RegWrite(RegWrite), .MemRead(MemRead), .MemToReg(MemToReg), .ALUSrc(ALUSrc), .MemWrite(MemWrite),
    .PCSrc(PCSrc));
  RegisterFile registerfile_1 (
    .WriteData(WriteData), .ResetRegs(in_1), .Clock(Clk), .RegWrite(RegWrite),
    .WriteRegAddr(multiplexer_1_out), .ReadReg1Addr(instructionmem_1_i25to21),
    .ReadReg2Addr(instructionmem_1_i20to16), .ReadReg1(registerfile_1_readreg1),
    .ReadReg2(registerfile_1_readreg2));
  // Probe on ALUOp
  // Probe on multiplexer_2_out
  // Probe on registerfile_1_readreg1
  Multiplexer #(.width(32)) multiplexer_2 (
    .in0(registerfile_1_readreg2), .in1(bit_extender_1_out), .out(multiplexer_2_out), .sel(ALUSrc));
  // Probe on registerfile_1_readreg2
  ALU alu_1 (
    .A(registerfile_1_readreg1), .B(multiplexer_2_out), .ALUOp(ALUOp), .Zero(alu_1_zero),
    .Result(alu_1_result));
  // Probe on alu_1_result
  // RAM #(.addrWidth(10), .databus("bidir"), .enables("line"), .line("quad"), .trigger("high")) ram_1: pin names not known; wires that end beside it: alu_1_result[9:0], MemWrite, MemRead, Clk, Clk, Clk, Clk, Clk
  assign controlled_buffer_1_out = MemRead ? {controlled_buffer_2_out_4, controlled_buffer_2_out_3, controlled_buffer_2_out_2, controlled_buffer_2_out} : 32'bz;  // Controlled_Buffer controlled_buffer_1
  assign {controlled_buffer_2_out_4, controlled_buffer_2_out_3, controlled_buffer_2_out_2, controlled_buffer_2_out} = MemWrite ? registerfile_1_readreg2 : 32'bz;  // Controlled_Buffer controlled_buffer_2
  // Probe on controlled_buffer_1_out
  // Probe on WriteData
  Multiplexer #(.width(32)) multiplexer_3 (
    .in0(alu_1_result), .in1(controlled_buffer_1_out), .out(WriteData), .sel(MemToReg));
endmodule

module PC (
  input  Clock,
  input  PCSrc,
  input  Reset,
  input  [15:0] BranchAddr,
  output [15:0] Address
);

  wire [15:0] fulladder16_1_s, fulladder16_2_s, multiplexer_1_out, shifter_1_out;

  Register #(.width(16)) register_1 (.D(multiplexer_1_out), .clk(Clock), .Q(Address), .clr(Reset));  // open: en
  Shifter #(.width(16)) shifter_1 (.in(BranchAddr), .\dist (4'b0010), .out(shifter_1_out));
  FullAdder16 fulladder16_1 (.X(Address), .Y(16'h4), .S(fulladder16_1_s));  // open: Cout
  // Probe on shifter_1_out
  Multiplexer #(.width(16)) multiplexer_1 (
    .in0(fulladder16_1_s), .in1(fulladder16_2_s), .out(multiplexer_1_out), .sel(PCSrc));
  FullAdder16 fulladder16_2 (.X(fulladder16_1_s), .Y(shifter_1_out), .S(fulladder16_2_s));  // open: Cout
endmodule

module RegisterFile (
  input  RegWrite,
  input  [31:0] WriteData,
  input  ResetRegs,
  input  [4:0] ReadReg1Addr,
  input  [4:0] ReadReg2Addr,
  input  [4:0] WriteRegAddr,
  input  Clock,
  output [31:0] ReadReg1,
  output [31:0] ReadReg2
);

  wire and_1_out, and_2_out, and_3_out, and_4_out, and_5_out, and_6_out, and_7_out, and_8_out, and_9_out,
       and_10_out, and_11_out, and_12_out, and_13_out, and_14_out, and_15_out, and_16_out, and_17_out,
       and_18_out, and_19_out, and_20_out, and_21_out, and_22_out, and_23_out, and_24_out, and_25_out,
       and_26_out, and_27_out, and_28_out, and_29_out, and_30_out, and_31_out, w0, w1, w2, w3, w4, w5, w6,
       w7, w8, w9, w10, w11, w12, w13, w14, w15, w16, w17, w18, w19, w20, w21, w22, w23, w24, w25, w26, w27,
       w28, w29, w30, w31;
  wire [31:0] r0, r1, r2, r3, r4, r5, r6, r7, r8, r9, r10, r11, r12, r13, r14, r15, r16, r17, r18, r19, r20,
       r21, r22, r23, r24, r25, r26, r27, r28, r29, r30, r31;

  and and_1 (and_1_out, RegWrite, w1);
  and and_2 (and_2_out, RegWrite, w2);
  and and_3 (and_3_out, RegWrite, w3);
  and and_4 (and_4_out, RegWrite, w4);
  and and_5 (and_5_out, RegWrite, w5);
  and and_6 (and_6_out, RegWrite, w6);
  and and_7 (and_7_out, RegWrite, w7);
  Register #(.width(32)) zero (.D(WriteData), .en(1'b0), .clk(Clock), .Q(r0), .clr(1'b0));
  Register #(.width(32)) at (.D(WriteData), .en(and_1_out), .clk(Clock), .Q(r1), .clr(ResetRegs));
  Register #(.width(32)) v0 (.D(WriteData), .en(and_2_out), .clk(Clock), .Q(r2), .clr(ResetRegs));
  Register #(.width(32)) v1 (.D(WriteData), .en(and_3_out), .clk(Clock), .Q(r3), .clr(ResetRegs));
  Register #(.width(32)) a0 (.D(WriteData), .en(and_4_out), .clk(Clock), .Q(r4), .clr(ResetRegs));
  Register #(.width(32)) a1 (.D(WriteData), .en(and_5_out), .clk(Clock), .Q(r5), .clr(ResetRegs));
  Register #(.width(32)) a2 (.D(WriteData), .en(and_6_out), .clk(Clock), .Q(r3), .clr(ResetRegs));
  Register #(.width(32)) a3 (.D(WriteData), .en(and_7_out), .clk(Clock), .Q(r7), .clr(ResetRegs));
  Register #(.width(32)) t0 (.D(WriteData), .en(and_8_out), .clk(Clock), .Q(r8), .clr(ResetRegs));
  and and_8 (and_8_out, RegWrite, w8);
  Register #(.width(32)) t1 (.D(WriteData), .en(and_9_out), .clk(Clock), .Q(r9), .clr(ResetRegs));
  and and_9 (and_9_out, RegWrite, w9);
  Register #(.width(32)) t2 (.D(WriteData), .en(and_10_out), .clk(Clock), .Q(r10), .clr(ResetRegs));
  and and_10 (and_10_out, RegWrite, w10);
  Register #(.width(32)) t3 (.D(WriteData), .en(and_11_out), .clk(Clock), .Q(r11), .clr(ResetRegs));
  and and_11 (and_11_out, RegWrite, w11);
  Register #(.width(32)) t4 (.D(WriteData), .en(and_12_out), .clk(Clock), .Q(r12), .clr(ResetRegs));
  and and_12 (and_12_out, RegWrite, w12);
  Register #(.width(32)) t5 (.D(WriteData), .en(and_13_out), .clk(Clock), .Q(r13), .clr(ResetRegs));
  and and_13 (and_13_out, RegWrite, w13);
  Register #(.width(32)) t6 (.D(WriteData), .en(and_14_out), .clk(Clock), .Q(r14), .clr(ResetRegs));
  and and_14 (and_14_out, RegWrite, w14);
  Register #(.width(32)) t7 (.D(WriteData), .en(and_15_out), .clk(Clock), .Q(r15), .clr(ResetRegs));
  and and_15 (and_15_out, RegWrite, w15);
  and and_16 (and_16_out, RegWrite, w16);
  and and_17 (and_17_out, RegWrite, w17);
  and and_18 (and_18_out, RegWrite, w18);
  and and_19 (and_19_out, RegWrite, w19);
  and and_20 (and_20_out, RegWrite, w20);
  and and_21 (and_21_out, RegWrite, w21);
  and and_22 (and_22_out, RegWrite, w22);
  and and_23 (and_23_out, RegWrite, w23);
  Register #(.width(32)) s0 (.D(WriteData), .en(and_16_out), .clk(Clock), .Q(r16), .clr(ResetRegs));
  Register #(.width(32)) s1 (.D(WriteData), .en(and_17_out), .clk(Clock), .Q(r17), .clr(ResetRegs));
  Register #(.width(32)) s2 (.D(WriteData), .en(and_18_out), .clk(Clock), .Q(r18), .clr(ResetRegs));
  Register #(.width(32)) s3 (.D(WriteData), .en(and_19_out), .clk(Clock), .Q(r19), .clr(ResetRegs));
  Register #(.width(32)) s4 (.D(WriteData), .en(and_20_out), .clk(Clock), .Q(r20), .clr(ResetRegs));
  Register #(.width(32)) s5 (.D(WriteData), .en(and_21_out), .clk(Clock), .Q(r21), .clr(ResetRegs));
  Register #(.width(32)) s6 (.D(WriteData), .en(and_22_out), .clk(Clock), .Q(r22), .clr(ResetRegs));
  Register #(.width(32)) s7 (.D(WriteData), .en(and_23_out), .clk(Clock), .Q(r23), .clr(ResetRegs));
  and and_24 (and_24_out, RegWrite, w24);
  and and_25 (and_25_out, RegWrite, w25);
  and and_26 (and_26_out, RegWrite, w26);
  and and_27 (and_27_out, RegWrite, w27);
  and and_28 (and_28_out, RegWrite, w28);
  and and_29 (and_29_out, RegWrite, w29);
  and and_30 (and_30_out, RegWrite, w30);
  and and_31 (and_31_out, RegWrite, w31);
  Register #(.width(32)) t8 (.D(WriteData), .en(and_24_out), .clk(Clock), .Q(r24), .clr(ResetRegs));
  Register #(.width(32)) t9 (.D(WriteData), .en(and_25_out), .clk(Clock), .Q(r25), .clr(ResetRegs));
  Register #(.width(32)) k0 (.D(WriteData), .en(and_26_out), .clk(Clock), .Q(r26), .clr(ResetRegs));
  Register #(.width(32)) k1 (.D(WriteData), .en(and_27_out), .clk(Clock), .Q(r27), .clr(ResetRegs));
  Register #(.width(32)) gp (.D(WriteData), .en(and_28_out), .clk(Clock), .Q(r28), .clr(ResetRegs));
  Register #(.width(32)) sp (.D(WriteData), .en(and_29_out), .clk(Clock), .Q(r29), .clr(ResetRegs));
  Register #(.width(32)) fp (.D(WriteData), .en(and_30_out), .clk(Clock), .Q(r30), .clr(ResetRegs));
  Register #(.width(32)) ra (.D(WriteData), .en(and_31_out), .clk(Clock), .Q(r31), .clr(ResetRegs));
  Multiplexer #(.select(5), .width(32)) multiplexer_1 (
    .in0(r0), .in1(r1), .in2(r2), .in3(r3), .in4(r4), .in5(r5), .in6(r6), .in7(r7), .in8(r8), .in9(r9),
    .in10(r10), .in11(r11), .in12(r12), .in13(r13), .in14(r14), .in15(r15), .in16(r16), .in17(r17),
    .in18(r18), .in19(r19), .in20(r20), .in21(r21), .in22(r22), .in23(r23), .in24(r24), .in25(r25),
    .in26(r26), .in27(r27), .in28(r28), .in29(r29), .in30(r30), .in31(r31), .out(ReadReg1), .sel(ReadReg1Addr));
  Demultiplexer #(.select(5)) demultiplexer_1 (
    .out0(w0), .out1(w1), .out2(w2), .out3(w3), .out4(w4), .out5(w5), .out6(w6), .out7(w7), .out8(w8),
    .out9(w9), .out10(w10), .out11(w11), .out12(w12), .out13(w13), .out14(w14), .out15(w15), .out16(w16),
    .out17(w17), .out18(w18), .out19(w19), .out20(w20), .out21(w21), .out22(w22), .out23(w23), .out24(w24),
    .out25(w25), .out26(w26), .out27(w27), .out28(w28), .out29(w29), .out30(w30), .out31(w31), .in(1'b1),
    .sel(WriteRegAddr));
  Multiplexer #(.select(5), .width(32)) multiplexer_2 (
    .in0(r0), .in1(r1), .in2(r2), .in3(r3), .in4(r4), .in5(r5), .in6(r6), .in7(r7), .in8(r8), .in9(r9),
    .in10(r10), .in11(r11), .in12(r12), .in13(r13), .in14(r14), .in15(r15), .in16(r16), .in17(r17),
    .in18(r18), .in19(r19), .in20(r20), .in21(r21), .in22(r22), .in23(r23), .in24(r24), .in25(r25),
    .in26(r26), .in27(r27), .in28(r28), .in29(r29), .in30(r30), .in31(r31), .out(ReadReg2), .sel(ReadReg2Addr));

  // Notes on the sheet:
  //   no writes here
endmodule

module InstructionMem (
  input  [15:0] Address,
  output [11:0] i31to26and5to0,
  output [4:0] i20to16,
  output [4:0] i25to21,
  output [15:0] i15To0,
  output [4:0] i15to11
);

  // ROM #(.addrWidth(16), .line("quad")) rom_1: pin names not known; wires that end beside it: Address, {i31to26and5to0[11:6], i25to21[4:3]}, {i25to21[2:0], i20to16}, i15To0[15:8], i15To0[7:0]
  // Probe on {i31to26and5to0[11:6], i25to21, i20to16, i15To0}

  assign i15to11 = i15To0[15:11];
  assign i31to26and5to0[5:0] = i15To0[5:0];

  // Notes on the sheet:
  //   contents of rom_1 (hex, n*v repeats v):
  //   8c 8 0 0 8c 9 0 4 8c a 0 8 8c b 0 c 8c c 0 10
endmodule

module ALU (
  input  [31:0] A,
  input  [31:0] B,
  input  [2:0] ALUOp,
  output Zero,
  output [31:0] Result
);

  wire bitselector_1_out, or_2_out;
  wire [31:0] and_1_out, bit_extender_1_out, fulladder32_1_s, fulladder32_2_s, not_1_out, or_1_out;

  assign not_1_out = ~B;  // NOT_Gate not_1, 32 bits wide
  assign and_1_out = A & B;  // AND_Gate and_1, 32 bits wide
  assign or_1_out = A | B;  // OR_Gate or_1, 32 bits wide
  FullAdder32 fulladder32_1 (.X(A), .Y(B), .S(fulladder32_1_s));  // open: Cin, Cout
  FullAdder32 fulladder32_2 (.Cin(1'b1), .X(A), .Y(not_1_out), .S(fulladder32_2_s));  // open: Cout
  BitSelector #(.width(32)) bitselector_1 (.in(fulladder32_2_s), .out(bitselector_1_out), .sel({5{1'b1}}));
  or or_2 (or_2_out, Result[31], Result[30], Result[29], Result[28], Result[27], Result[26], Result[25], Result[24], Result[23], Result[22], Result[21], Result[20], Result[19], Result[18], Result[17], Result[16], Result[14], Result[13], Result[12], Result[11], Result[10], Result[9], Result[8], Result[7], Result[6], Result[5], Result[4], Result[3], Result[2], Result[1], Result[0], Result[15]);
  assign bit_extender_1_out = {{31{bitselector_1_out}}, bitselector_1_out};  // Bit_Extender bit_extender_1
  not not_2 (Zero, or_2_out);
  Multiplexer #(.select(3), .width(32)) multiplexer_1 (
    .in0(and_1_out), .in1(or_1_out), .in2(fulladder32_1_s), .in6(fulladder32_2_s), .in7(bit_extender_1_out),
    .out(Result), .sel(ALUOp));  // open: in3, in4, in5
endmodule

module Control (
  input  [11:0] OPCODEFUNC,
  input  Zero,
  output [2:0] ALUOp,
  output RegDst,
  output RegWrite,
  output MemRead,
  output MemToReg,
  output ALUSrc,
  output MemWrite,
  output PCSrc
);

  wire ADDF_out, ADDI_out, ANDF_out, ANDI_out, BEQ_out, IMM_out, ORF_out, ORI_out, RT_out, SLTI_out, SUBF_out;
  wire [2:0] multiplexer_1_out, multiplexer_2_out, multiplexer_3_out, multiplexer_4_out, multiplexer_5_out;
  wire [5:0] demultiplexer_1_out0, demultiplexer_1_out1;

  // NoConnect on demultiplexer_1_out0
  Demultiplexer #(.width(6)) demultiplexer_1 (
    .out0(demultiplexer_1_out0), .out1(demultiplexer_1_out1), .in(OPCODEFUNC[5:0]), .sel(RegDst));
  and ADDF (ADDF_out, ~demultiplexer_1_out1[0], ~demultiplexer_1_out1[1], ~demultiplexer_1_out1[2], ~demultiplexer_1_out1[3], ~demultiplexer_1_out1[4], demultiplexer_1_out1[5]);  // AND_Gate
  and SUBF (SUBF_out, ~demultiplexer_1_out1[0], demultiplexer_1_out1[1], ~demultiplexer_1_out1[2], ~demultiplexer_1_out1[3], ~demultiplexer_1_out1[4], demultiplexer_1_out1[5]);  // AND_Gate
  and ANDF (ANDF_out, ~demultiplexer_1_out1[0], ~demultiplexer_1_out1[1], demultiplexer_1_out1[2], ~demultiplexer_1_out1[3], ~demultiplexer_1_out1[4], demultiplexer_1_out1[5]);  // AND_Gate
  and ORF (ORF_out, demultiplexer_1_out1[0], ~demultiplexer_1_out1[1], demultiplexer_1_out1[2], ~demultiplexer_1_out1[3], ~demultiplexer_1_out1[4], demultiplexer_1_out1[5]);  // AND_Gate
  or RT (RT_out, OPCODEFUNC[6], OPCODEFUNC[7], OPCODEFUNC[8], OPCODEFUNC[9], OPCODEFUNC[10], OPCODEFUNC[11]);
  not not_1 (RegDst, RT_out);
  and LW (MemRead, OPCODEFUNC[6], OPCODEFUNC[7], ~OPCODEFUNC[8], ~OPCODEFUNC[9], ~OPCODEFUNC[10], OPCODEFUNC[11]);  // AND_Gate
  and SW (MemWrite, OPCODEFUNC[6], OPCODEFUNC[7], ~OPCODEFUNC[8], OPCODEFUNC[9], ~OPCODEFUNC[10], OPCODEFUNC[11]);  // AND_Gate
  and BEQ (BEQ_out, ~OPCODEFUNC[6], ~OPCODEFUNC[7], OPCODEFUNC[8], ~OPCODEFUNC[9], ~OPCODEFUNC[10], ~OPCODEFUNC[11]);  // AND_Gate
  or IMM (IMM_out, ADDI_out, ANDI_out, ORI_out, SLTI_out);
  and ADDI (ADDI_out, ~OPCODEFUNC[6], ~OPCODEFUNC[7], ~OPCODEFUNC[8], OPCODEFUNC[9], ~OPCODEFUNC[10], ~OPCODEFUNC[11]);  // AND_Gate
  and ANDI (ANDI_out, ~OPCODEFUNC[6], ~OPCODEFUNC[7], OPCODEFUNC[8], OPCODEFUNC[9], ~OPCODEFUNC[10], ~OPCODEFUNC[11]);  // AND_Gate
  and ORI (ORI_out, OPCODEFUNC[6], ~OPCODEFUNC[7], OPCODEFUNC[8], OPCODEFUNC[9], ~OPCODEFUNC[10], ~OPCODEFUNC[11]);  // AND_Gate
  and SLTI (SLTI_out, ~OPCODEFUNC[6], OPCODEFUNC[7], ~OPCODEFUNC[8], OPCODEFUNC[9], ~OPCODEFUNC[10], ~OPCODEFUNC[11]);  // AND_Gate
  Multiplexer #(.width(3)) multiplexer_1 (.in0(3'b111), .in1(3'b010), .out(multiplexer_1_out), .sel(ADDF_out));
  Multiplexer #(.width(3)) multiplexer_2 (
    .in0(multiplexer_1_out), .in1(3'b110), .out(multiplexer_2_out), .sel(SUBF_out));
  Multiplexer #(.width(3)) multiplexer_3 (
    .in0(multiplexer_2_out), .in1(3'b000), .out(multiplexer_3_out), .sel(ANDF_out));
  Multiplexer #(.width(3)) multiplexer_4 (
    .in0(multiplexer_3_out), .in1(3'b001), .out(multiplexer_4_out), .sel(ORF_out));
  Multiplexer #(.width(3)) multiplexer_5 (.in0(multiplexer_4_out), .in1(3'b010), .out(multiplexer_5_out), .sel(ALUSrc));
  Multiplexer #(.width(3)) multiplexer_6 (.in0(multiplexer_5_out), .in1(3'b110), .out(ALUOp), .sel(BEQ_out));
  or or_1 (RegWrite, RegDst, MemRead, IMM_out);
  or or_2 (ALUSrc, MemRead, MemWrite, IMM_out);
  and BEQZ (PCSrc, BEQ_out, Zero);

  assign MemToReg = MemRead;

  // Notes on the sheet:
  //   FUNC
  //   OPCODE
  //   To ignore func codes unless R-type
endmodule
