// Logisim project RegisterFile.circ as structural Verilog: 2 circuits, main circuit Register32
module Register32 (
  input  Clock,
  input  [31:0] D,
  output [31:0] Q,
  output [31:0] Qn
);

  DFlipFlop dflipflop_1 (.D(D[0]), .En(Clock), .Q(Q[0]), .Qn(Qn[0]));
  DFlipFlop dflipflop_2 (.D(D[1]), .En(Clock), .Q(Q[1]), .Qn(Qn[1]));
  DFlipFlop dflipflop_3 (.D(D[2]), .En(Clock), .Q(Q[2]), .Qn(Qn[2]));
  DFlipFlop dflipflop_4 (.D(D[3]), .En(Clock), .Q(Q[3]), .Qn(Qn[3]));
  DFlipFlop dflipflop_5 (.D(D[4]), .En(Clock), .Q(Q[4]), .Qn(Qn[4]));
  DFlipFlop dflipflop_6 (.D(D[5]), .En(Clock), .Q(Q[5]), .Qn(Qn[5]));
  DFlipFlop dflipflop_7 (.D(D[6]), .En(Clock), .Q(Q[6]), .Qn(Qn[6]));
  DFlipFlop dflipflop_8 (.D(D[7]), .En(Clock), .Q(Q[7]), .Qn(Qn[7]));
  DFlipFlop dflipflop_9 (.D(D[8]), .En(Clock), .Q(Q[8]), .Qn(Qn[8]));
  DFlipFlop dflipflop_10 (.D(D[9]), .En(Clock), .Q(Q[9]), .Qn(Qn[9]));
  DFlipFlop dflipflop_11 (.D(D[10]), .En(Clock), .Q(Q[10]), .Qn(Qn[10]));
  DFlipFlop dflipflop_12 (.D(D[11]), .En(Clock), .Q(Q[11]), .Qn(Qn[11]));
  DFlipFlop dflipflop_13 (.D(D[12]), .En(Clock), .Q(Q[12]), .Qn(Qn[12]));
  DFlipFlop dflipflop_14 (.D(D[13]), .En(Clock), .Q(Q[13]), .Qn(Qn[13]));
  DFlipFlop dflipflop_15 (.D(D[14]), .En(Clock), .Q(Q[14]), .Qn(Qn[14]));
  DFlipFlop dflipflop_16 (.D(D[15]), .En(Clock), .Q(Q[15]), .Qn(Qn[15]));
  DFlipFlop dflipflop_17 (.D(D[16]), .En(Clock), .Q(Q[16]), .Qn(Qn[16]));
  DFlipFlop dflipflop_18 (.D(D[17]), .En(Clock), .Q(Q[17]), .Qn(Qn[17]));
  DFlipFlop dflipflop_19 (.D(D[18]), .En(Clock), .Q(Q[18]), .Qn(Qn[18]));
  DFlipFlop dflipflop_20 (.D(D[19]), .En(Clock), .Q(Q[19]), .Qn(Qn[19]));
  DFlipFlop dflipflop_21 (.D(D[20]), .En(Clock), .Q(Q[20]), .Qn(Qn[20]));
  DFlipFlop dflipflop_22 (.D(D[21]), .En(Clock), .Q(Q[21]), .Qn(Qn[21]));
  DFlipFlop dflipflop_23 (.D(D[22]), .En(Clock), .Q(Q[22]), .Qn(Qn[22]));
  DFlipFlop dflipflop_24 (.D(D[23]), .En(Clock), .Q(Q[23]), .Qn(Qn[23]));
  DFlipFlop dflipflop_25 (.D(D[24]), .En(Clock), .Q(Q[24]), .Qn(Qn[24]));
  DFlipFlop dflipflop_26 (.D(D[25]), .En(Clock), .Q(Q[25]), .Qn(Qn[25]));
  DFlipFlop dflipflop_27 (.D(D[26]), .En(Clock), .Q(Q[26]), .Qn(Qn[26]));
  DFlipFlop dflipflop_28 (.D(D[27]), .En(Clock), .Q(Q[27]), .Qn(Qn[27]));
  DFlipFlop dflipflop_29 (.D(D[28]), .En(Clock), .Q(Q[28]), .Qn(Qn[28]));
  DFlipFlop dflipflop_30 (.D(D[29]), .En(Clock), .Q(Q[29]), .Qn(Qn[29]));
  DFlipFlop dflipflop_31 (.D(D[30]), .En(Clock), .Q(Q[30]), .Qn(Qn[30]));
  DFlipFlop dflipflop_32 (.D(D[31]), .En(Clock), .Q(Q[31]), .Qn(Qn[31]));
endmodule

module RegisterFile32 (
  input  [31:0] ReadReg1,
  input  [31:0] ReadReg2,
  input  [4:0] ReadReg1Addr,
  input  [4:0] ReadReg2Addr,
  input  Clock,
  input  [4:0] WriteRegAddr,
  output [31:0] WriteReg
);

  wire [31:0] r0, r1, r2, r3, r4, r5, r6, r7, r8, r9, r10, r11, r12, r13, r14, r15, r16, r17, r18, r19, r20,
       r21, r22, r23, r24, r25, r26, r27, r28, r29, r30, r31, w0, w1, w2, w3, w4, w5, w6, w7, w8, w9, w10,
       w11, w12, w13, w14, w15, w16, w17, w18, w19, w20, w21, w22, w23, w24, w25, w26, w27, w28, w29, w30,
       w31;

  Multiplexer #(.select(5), .width(32)) multiplexer_1 (
    .in0(r0), .in1(r1), .in2(r2), .in3(r3), .in4(r4), .in5(r5), .in6(r6), .in7(r7), .in8(r8), .in9(r9),
    .in10(r10), .in11(r11), .in12(r12), .in13(r13), .in14(r14), .in15(r15), .in16(r16), .in17(r17),
    .in18(r18), .in19(r19), .in20(r20), .in21(r21), .in22(r22), .in23(r23), .in24(r24), .in25(r25),
    .in26(r26), .in27(r27), .in28(r28), .in29(r29), .in30(r30), .in31(r31), .out(ReadReg1), .sel(ReadReg1Addr));
  Demultiplexer #(.select(5), .width(32)) demultiplexer_1 (
    .out0(w0), .out1(w1), .out2(w2), .out3(w3), .out4(w4), .out5(w5), .out6(w6), .out7(w7), .out8(w8),
    .out9(w9), .out10(w10), .out11(w11), .out12(w12), .out13(w13), .out14(w14), .out15(w15), .out16(w16),
    .out17(w17), .out18(w18), .out19(w19), .out20(w20), .out21(w21), .out22(w22), .out23(w23), .out24(w24),
    .out25(w25), .out26(w26), .out27(w27), .out28(w28), .out29(w29), .out30(w30), .out31(w31), .in(WriteReg),
    .sel(WriteRegAddr));
  Register32 register32_1 (.Clock(Clock), .D(w0), .Q(r0));  // open: Qn
  Register32 register32_2 (.Clock(Clock), .D(w1), .Q(r1));  // open: Qn
  Register32 register32_3 (.Clock(Clock), .D(w2), .Q(r2));  // open: Qn
  Register32 register32_4 (.Clock(Clock), .D(w3), .Q(r3));  // open: Qn
  Register32 register32_5 (.Clock(Clock), .D(w4), .Q(r4));  // open: Qn
  Register32 register32_6 (.Clock(Clock), .D(w5), .Q(r5));  // open: Qn
  Register32 register32_7 (.Clock(Clock), .D(w6), .Q(r3));  // open: Qn
  Register32 register32_8 (.Clock(Clock), .D(w7), .Q(r7));  // open: Qn
  Register32 register32_9 (.Clock(Clock), .D(w8), .Q(r8));  // open: Qn
  Register32 register32_10 (.Clock(Clock), .D(w9), .Q(r9));  // open: Qn
  Register32 register32_11 (.Clock(Clock), .D(w10), .Q(r10));  // open: Qn
  Register32 register32_12 (.Clock(Clock), .D(w11), .Q(r11));  // open: Qn
  Register32 register32_13 (.Clock(Clock), .D(w12), .Q(r12));  // open: Qn
  Register32 register32_14 (.Clock(Clock), .D(w13), .Q(r13));  // open: Qn
  Register32 register32_15 (.Clock(Clock), .D(w14), .Q(r14));  // open: Qn
  Register32 register32_16 (.Clock(Clock), .D(w15), .Q(r15));  // open: Qn
  Register32 register32_17 (.Clock(Clock), .D(w16), .Q(r16));  // open: Qn
  Register32 register32_18 (.Clock(Clock), .D(w17), .Q(r17));  // open: Qn
  Register32 register32_19 (.Clock(Clock), .D(w18), .Q(r18));  // open: Qn
  Register32 register32_20 (.Clock(Clock), .D(w19), .Q(r19));  // open: Qn
  Register32 register32_21 (.Clock(Clock), .D(w20), .Q(r20));  // open: Qn
  Register32 register32_22 (.Clock(Clock), .D(w21), .Q(r21));  // open: Qn
  Register32 register32_23 (.Clock(Clock), .D(w22), .Q(r22));  // open: Qn
  Register32 register32_24 (.Clock(Clock), .D(w23), .Q(r23));  // open: Qn
  Multiplexer #(.select(5), .width(32)) multiplexer_2 (
    .in0(r0), .in1(r1), .in2(r2), .in3(r3), .in4(r4), .in5(r5), .in6(r6), .in7(r7), .in8(r8), .in9(r9),
    .in10(r10), .in11(r11), .in12(r12), .in13(r13), .in14(r14), .in15(r15), .in16(r16), .in17(r17),
    .in18(r18), .in19(r19), .in20(r20), .in21(r21), .in22(r22), .in23(r23), .in24(r24), .in25(r25),
    .in26(r26), .in27(r27), .in28(r28), .in29(r29), .in30(r30), .in31(r31), .out(ReadReg2), .sel(ReadReg2Addr));
  Register32 register32_25 (.Clock(Clock), .D(w24), .Q(r24));  // open: Qn
  Register32 register32_26 (.Clock(Clock), .D(w25), .Q(r25));  // open: Qn
  Register32 register32_27 (.Clock(Clock), .D(w26), .Q(r26));  // open: Qn
  Register32 register32_28 (.Clock(Clock), .D(w27), .Q(r27));  // open: Qn
  Register32 register32_29 (.Clock(Clock), .D(w28), .Q(r28));  // open: Qn
  Register32 register32_30 (.Clock(Clock), .D(w29), .Q(r29));  // open: Qn
  Register32 register32_31 (.Clock(Clock), .D(w30), .Q(r30));  // open: Qn
  Register32 register32_32 (.Clock(Clock), .D(w31), .Q(r31));  // open: Qn
endmodule
